// Logisim project LIB_74XX_IC_family.circ as structural Verilog: 14 circuits, main circuit IC_74574
module IC_74574 (
  input  [7:0] D,
  input  CP,
  input  OE,
  output [7:0] O,
  output [7:0] val
);

  wire not_1_out;

  Register register_1 (.D(D), .Q(val), .clk(CP));  // open: en, clr
  not not_1 (not_1_out, OE);
  assign O = not_1_out ? val : 8'bz;  // Controlled_Buffer controlled_buffer_1
endmodule

module IC_74161 (
  input  LD,
  input  [3:0] D,
  input  CLK,
  input  CLR,
  input  ENT,
  input  ENP,
  output [3:0] val,
  output [3:0] Q,
  output CO
);

  wire and_1_out, counter_1_carry, not_1_out, not_2_out;

  not not_1 (not_1_out, LD);
  not not_2 (not_2_out, CLR);
  and and_1 (and_1_out, ENT, ENP);
  Counter #(.max('hf), .width(4)) counter_1 (
    .load(not_1_out), .D(D), .count(and_1_out), .Q(Q), .carry(counter_1_carry), .clk(CLK), .clr(not_2_out));  // open: up
  and and_2 (CO, counter_1_carry, ENT);

  assign val = Q;
endmodule

module IC_74670 (
  input  RE,
  input  [1:0] RA,
  input  [1:0] WA,
  input  WE,
  input  [3:0] D,
  output [3:0] val3,
  output [3:0] val2,
  output [3:0] Q,
  output [3:0] val1,
  output [3:0] val0
);

  wire buffer_1_out, buffer_2_out, buffer_3_out, buffer_4_out, buffer_5_out, buffer_6_out, buffer_7_out,
       buffer_8_out, buffer_9_out, buffer_10_out, buffer_11_out, buffer_12_out, buffer_13_out, buffer_14_out,
       buffer_15_out, buffer_16_out, buffer_17_out, buffer_18_out, buffer_19_out, buffer_20_out,
       buffer_21_out, buffer_22_out, buffer_23_out, buffer_24_out, buffer_25_out, buffer_26_out,
       buffer_27_out, buffer_28_out, decoder_1_out0, decoder_1_out1, decoder_1_out2, decoder_1_out3,
       decoder_2_out0, decoder_2_out1, decoder_2_out2, decoder_2_out3, not_1_out;

  buf buffer_1 (buffer_1_out, WE);
  buf buffer_2 (buffer_2_out, buffer_1_out);
  buf buffer_3 (buffer_3_out, buffer_2_out);
  buf buffer_4 (buffer_4_out, buffer_3_out);
  buf buffer_5 (buffer_5_out, buffer_4_out);
  buf buffer_6 (buffer_6_out, buffer_5_out);
  buf buffer_7 (buffer_7_out, buffer_6_out);
  buf buffer_8 (buffer_8_out, buffer_7_out);
  not not_1 (not_1_out, RE);
  Decoder #(.enable("false"), .select(2)) decoder_1 (
    .out0(decoder_1_out0), .out1(decoder_1_out1), .out2(decoder_1_out2), .out3(decoder_1_out3), .sel(WA));
  buf buffer_9 (buffer_9_out, decoder_1_out0);
  buf buffer_10 (buffer_10_out, decoder_1_out1);
  buf buffer_11 (buffer_11_out, decoder_1_out2);
  buf buffer_12 (buffer_12_out, decoder_1_out3);
  buf buffer_13 (buffer_13_out, buffer_9_out);
  buf buffer_14 (buffer_14_out, buffer_10_out);
  buf buffer_15 (buffer_15_out, buffer_11_out);
  buf buffer_16 (buffer_16_out, buffer_12_out);
  buf buffer_17 (buffer_17_out, buffer_13_out);
  buf buffer_18 (buffer_18_out, buffer_14_out);
  buf buffer_19 (buffer_19_out, buffer_15_out);
  buf buffer_20 (buffer_20_out, buffer_16_out);
  buf buffer_21 (buffer_21_out, buffer_17_out);
  buf buffer_22 (buffer_22_out, buffer_18_out);
  buf buffer_23 (buffer_23_out, buffer_19_out);
  buf buffer_24 (buffer_24_out, buffer_20_out);
  buf buffer_25 (buffer_25_out, buffer_21_out);
  buf buffer_26 (buffer_26_out, buffer_22_out);
  buf buffer_27 (buffer_27_out, buffer_23_out);
  buf buffer_28 (buffer_28_out, buffer_24_out);
  Register #(.trigger("low"), .width(4)) register_1 (
    .D(D), .en(buffer_28_out), .Q(val3), .clk(buffer_8_out));  // open: clr
  Register #(.trigger("low"), .width(4)) register_2 (
    .D(D), .en(buffer_27_out), .Q(val2), .clk(buffer_8_out));  // open: clr
  Register #(.trigger("low"), .width(4)) register_3 (
    .D(D), .en(buffer_26_out), .Q(val1), .clk(buffer_8_out));  // open: clr
  Register #(.trigger("low"), .width(4)) register_4 (
    .D(D), .en(buffer_25_out), .Q(val0), .clk(buffer_8_out));  // open: clr
  Decoder #(.select(2)) decoder_2 (
    .out0(decoder_2_out0), .out1(decoder_2_out1), .out2(decoder_2_out2), .out3(decoder_2_out3), .sel(RA),
    .en(not_1_out));
  assign Q = decoder_2_out3 ? val3 : 4'bz;  // Controlled_Buffer controlled_buffer_1
  assign Q = decoder_2_out2 ? val2 : 4'bz;  // Controlled_Buffer controlled_buffer_2
  assign Q = decoder_2_out1 ? val1 : 4'bz;  // Controlled_Buffer controlled_buffer_3
  assign Q = decoder_2_out0 ? val0 : 4'bz;  // Controlled_Buffer controlled_buffer_4
endmodule

module IC_74138 (
  input  EN1,
  input  EN2,
  input  EN3,
  input  [2:0] D,
  output Y0,
  output Y1,
  output Y2,
  output Y3,
  output Y4,
  output Y5,
  output Y6,
  output Y7
);

  wire and_1_out, decoder_1_out0, decoder_1_out1, decoder_1_out2, decoder_1_out3, decoder_1_out4,
       decoder_1_out5, decoder_1_out6, decoder_1_out7, not_1_out, not_2_out;

  not not_1 (not_1_out, EN2);
  not not_2 (not_2_out, EN3);
  and and_1 (and_1_out, EN1, not_1_out, not_2_out);
  Decoder #(.select(3)) decoder_1 (
    .out0(decoder_1_out0), .out1(decoder_1_out1), .out2(decoder_1_out2), .out3(decoder_1_out3),
    .out4(decoder_1_out4), .out5(decoder_1_out5), .out6(decoder_1_out6), .out7(decoder_1_out7), .sel(D),
    .en(and_1_out));
  not not_3 (Y0, decoder_1_out0);
  not not_4 (Y1, decoder_1_out1);
  not not_5 (Y2, decoder_1_out2);
  not not_6 (Y3, decoder_1_out3);
  not not_7 (Y4, decoder_1_out4);
  not not_8 (Y5, decoder_1_out5);
  not not_9 (Y6, decoder_1_out6);
  not not_10 (Y7, decoder_1_out7);
endmodule

module IC_7400 (
  input  A,
  input  B,
  output Q
);

  nand nand_1 (Q, A, B);
endmodule

module IC_7408 (
  input  A,
  input  B,
  output Q
);

  and and_1 (Q, A, B);
endmodule

module IC_74283 (
  input  CIN,
  input  [3:0] A,
  input  [3:0] B,
  output [3:0] val,
  output [3:0] SUM,
  output CO
);

  Adder #(.width(4)) adder_1 (.a(A), .b(B), .out(SUM), .cin(CIN), .cout(CO));

  assign val = SUM;
endmodule

module IC_74541 (
  input  [7:0] I,
  input  OE1,
  input  OE2,
  output [7:0] Y
);

  wire and_1_out, not_1_out, not_2_out;

  not not_1 (not_1_out, OE1);
  not not_2 (not_2_out, OE2);
  and and_1 (and_1_out, not_1_out, not_2_out);
  assign Y = and_1_out ? I : 8'bz;  // Controlled_Buffer controlled_buffer_1
endmodule

module IC_74151 (
  input  EN,
  input  [2:0] S,
  input  D0,
  input  D1,
  input  D2,
  input  D3,
  input  D4,
  input  D5,
  input  D6,
  input  D7,
  output Y,
  output W
);

  wire not_1_out;

  not not_1 (not_1_out, EN);
  Multiplexer #(.enable("true"), .select(3)) multiplexer_1 (
    .in0(D0), .in1(D1), .in2(D2), .in3(D3), .in4(D4), .in5(D5), .in6(D6), .in7(D7), .out(Y), .sel(S),
    .en(not_1_out));
  not not_2 (W, Y);
endmodule

module IC_74181 (
  input  [3:0] A,
  input  [3:0] B,
  input  [3:0] S,
  input  CIN,
  input  M,
  output G,
  output CO,
  output P,
  output AEQB,
  output [3:0] val,
  output [3:0] F
);

  wire buffer_1_out, buffer_2_out, buffer_3_out, buffer_4_out, n74181_1_p13;

  // _74181 #(.ShowInternalStructure("true")) 74181_1: pin names not known; wires that end beside it: B[0], A[1], A[0], B[1], S[3], A[2], S[2], B[2], S[1], A[3], S[0], B[3], n74181_1_p13, G, M, CO, F[0], P, F[1], AEQB, F[2], F[3]
  buf buffer_1 (buffer_1_out, CIN);
  buf buffer_2 (buffer_2_out, buffer_1_out);
  buf buffer_3 (buffer_3_out, buffer_2_out);
  buf buffer_4 (buffer_4_out, buffer_3_out);
  and and_1 (n74181_1_p13, buffer_4_out, CIN);

  assign val = F;
endmodule

module IC_74688 (
  input  [7:0] P,
  input  [7:0] Q,
  input  G,
  output val,
  output EQ
);

  wire comparator_1_eq, not_1_out;

  Comparator #(.mode("unsigned")) comparator_1 (.a(P), .b(Q), .eq(comparator_1_eq));  // open: gt, lt
  not not_1 (not_1_out, G);
  not not_2 (val, comparator_1_eq);
  nand nand_1 (EQ, comparator_1_eq, not_1_out);
endmodule

module IC_7432 (
  input  A,
  input  B,
  output Q
);

  or or_1 (Q, A, B);
endmodule

module IC_7406 (
  input  A,
  output Q
);

  not not_1 (Q, A);
endmodule

module RESISTOR (
  input  R_IN,
  input  R_OUT_B,
  output R_OUT_A
);

  assign R_OUT_A = R_OUT_B ? R_IN : 1'bz;  // Controlled_Buffer controlled_buffer_1
endmodule
