// Logisim project LIB_Jednostava_CPU.circ as structural Verilog: 2 circuits, main circuit Jednostava16_CPU
module Jednostava16_CPU (
  input  INTL,
  input  [15:0] BUS_DATA_IN,
  input  CLK_EN,
  input  CLK,
  input  INT_0,
  input  INT_1,
  input  INT_2,
  input  INT_3,
  input  INT_4,
  input  INT_5,
  input  INT_6,
  input  INT_7,
  output [7:0] out_13,
  output [7:0] out_14,
  output [3:0] out_15,
  output [3:0] out_16,
  output [7:0] out_17,
  output [7:0] BUS_SCT,
  output [3:0] out_19,
  output [3:0] out_20,
  output [3:0] out_21,
  output [7:0] out_22,
  output [3:0] out_23,
  output [3:0] out_24,
  output [3:0] out_25,
  output [7:0] out_26,
  output [3:0] out_27,
  output [3:0] out_28,
  output [7:0] out_29,
  output [7:0] out_30,
  output [3:0] out_31,
  output [7:0] out_32,
  output [3:0] out_33,
  output [15:0] BUS_DATA_OUT,
  output W,
  output [3:0] out_36,
  output [3:0] out_37,
  output [3:0] out_38,
  output [3:0] out_39,
  output [15:0] BUS_ADR,
  output [3:0] out_41,
  output [3:0] out_42,
  output [3:0] out_43,
  output [3:0] out_44,
  output [3:0] out_45,
  output [3:0] out_46,
  output [3:0] out_47,
  output [3:0] out_48,
  output [3:0] out_49,
  output [3:0] out_50,
  output [3:0] out_51,
  output [3:0] out_52,
  output R,
  output [3:0] out_54,
  output [3:0] out_55,
  output CLK_T8,
  output [3:0] out_57,
  output [3:0] out_58,
  output [3:0] out_59,
  output [3:0] out_60,
  output [3:0] out_61,
  output CLK_T16,
  output [3:0] out_63,
  output [3:0] out_64,
  output CLK_T1,
  output [3:0] out_66,
  output [3:0] out_67,
  output [3:0] out_68,
  output [3:0] out_69,
  output [3:0] out_70,
  output [3:0] out_71,
  output [3:0] out_72,
  output [3:0] out_73,
  output [7:0] out_74,
  output [3:0] out_75,
  output INTM
);

  wire ACT_ALU_CIN, ACT_DV_H, ACT_DV_L, ACT_INT_E, ACT_INT_S, ACT_OP_CIN, ACT_OUTPUT_M, ACT_PF,
       ALU_ALU_HL_co, ALU_ALU_LH_co, ALU_ALU_LL_co, FLG_CO, FLG_EQU_HH, FLG_EQU_HL, FLG_EQU_LH, FLG_EQU_LL,
       FLG_NEG, IEU_NAND_A_q, IEU_NAND_B_q, IEU_NAND_D_q, JCU_NAND_A_q, JCU_NAND_B_q, JCU_NAND_C_q, OPC_A,
       OPC_DVR, OPC_INTC, OPC_JCR, OPC_PF, OPC_RF, OPC_SF, SCU_AND_C_q, SRC_ADRD, SRC_DVR, SRC_INTB, SRC_PF,
       SRC_RF, SRC_SF, STEP_1, STEP_2, STEP_3, STEP_4, STEP_5, STEP_6, STEP_7, STEP_CNTI_M, STEP_IGR,
       STEP_IMR, STEP_OPCE, STEP_SRCR;
  wire [0:0] JCU_MUL_w;
  wire [1:0] BUS_ARGO, BUS_ARGS, BUS_FRA, BUS_FWA;
  wire [2:0] ALU_ALU_HH_f, SCU_CNT_q;
  wire [3:0] ALU_ALU_HL_f, ALU_ALU_LH_f, ALU_ALU_LL_f;
  wire [4:0] BUS_OP;
  wire [7:0] ALU_REG_A_H_o, ALU_REG_A_L_o, IEU_REG_I_H_o, JCU_REG_o;
  wire [7:4] IC_BUF_IM_y, IC_BUF_SRC_y;
  wire [15:0] BUS_DATA_IN_t, BUS_DATA_OUT_t;

  IC_7408 JCU_NAND_A (.A(FLG_EQU_LL), .B(FLG_EQU_LH), .Q(JCU_NAND_A_q));
  IC_7408 JCU_NAND_B (.A(FLG_EQU_HL), .B(FLG_EQU_HH), .Q(JCU_NAND_B_q));
  IC_74574 ALU_REG_A_L (.D(BUS_DATA_IN_t[7:0]), .CP(OPC_A), .OE(1'b0), .O(ALU_REG_A_L_o), .val(out_29));
  IC_74574 ALU_REG_A_H (.D(BUS_DATA_IN_t[15:8]), .CP(OPC_A), .OE(1'b0), .O(ALU_REG_A_H_o), .val(out_32));
  IC_7408 JCU_NAND_C (.A(JCU_NAND_A_q), .B(JCU_NAND_B_q), .Q(JCU_NAND_C_q));
  IC_74670 RF_FILE_LL (
    .RA(BUS_FRA), .WA(BUS_FWA), .WE(OPC_RF), .D(BUS_DATA_OUT_t[3:0]), .RE(SRC_RF), .val3(out_43),
    .val2(out_41), .Q(BUS_DATA_IN_t[3:0]), .val1(out_38), .val0(out_36));
  IC_74670 RF_FILE_LH (
    .RA(BUS_FRA), .WA(BUS_FRA), .WE(OPC_RF), .D(BUS_DATA_OUT_t[7:4]), .RE(SRC_RF), .val3(out_51),
    .val2(out_49), .Q(BUS_DATA_IN_t[7:4]), .val1(out_47), .val0(out_45));
  IC_74670 RF_FILE_HL (
    .RA(BUS_FRA), .WA(BUS_FWA), .WE(OPC_RF), .D(BUS_DATA_OUT_t[11:8]), .RE(SRC_RF), .val3(out_63),
    .val2(out_60), .Q(BUS_DATA_IN_t[11:8]), .val1(out_57), .val0(out_54));
  IC_74670 RF_FILE_HH (
    .RA(BUS_FRA), .WA(BUS_FWA), .WE(OPC_RF), .D(BUS_DATA_OUT_t[15:12]), .RE(SRC_RF), .val3(out_72),
    .val2(out_70), .Q(BUS_DATA_IN_t[15:12]), .val1(out_68), .val0(out_66));
  IC_74151 JCU_MUL (
    .S({1'b1, BUS_ARGO}), .D0(FLG_NEG), .D1(FLG_CO), .D2(JCU_NAND_C_q), .D3(INTM), .D4(1'b1), .D5(1'b1),
    .D6(1'b1), .D7(1'b1), .EN(1'b0), .W(JCU_MUL_w[0]));  // open: Y
  IC_74181 ALU_ALU_LL (
    .CIN(ACT_ALU_CIN), .M(BUS_OP[4]), .A(BUS_DATA_IN_t[3:0]), .S(BUS_OP[3:0]), .B(ALU_REG_A_L_o[3:0]),
    .AEQB(FLG_EQU_LL), .CO(ALU_ALU_LL_co), .val(out_20), .F(ALU_ALU_LL_f));  // open: G, P
  IC_74181 ALU_ALU_LH (
    .CIN(ALU_ALU_LL_co), .M(BUS_OP[4]), .A(BUS_DATA_IN_t[7:4]), .S(BUS_OP[3:0]), .B(ALU_REG_A_L_o[7:4]),
    .AEQB(FLG_EQU_LH), .CO(ALU_ALU_LH_co), .val(out_28), .F(ALU_ALU_LH_f));  // open: G, P
  IC_74181 ALU_ALU_HL (
    .CIN(ALU_ALU_LH_co), .M(BUS_OP[4]), .A(BUS_DATA_IN_t[11:8]), .S(BUS_OP[3:0]), .B(ALU_REG_A_H_o[3:0]),
    .AEQB(FLG_EQU_HL), .CO(ALU_ALU_HL_co), .val(out_31), .F(ALU_ALU_HL_f));  // open: G, P
  IC_74181 ALU_ALU_HH (
    .CIN(ALU_ALU_HL_co), .M(BUS_OP[4]), .A(BUS_DATA_IN_t[15:12]), .S(BUS_OP[3:0]), .B(ALU_REG_A_H_o[7:4]),
    .AEQB(FLG_EQU_HH), .CO(FLG_CO), .val(out_33), .F({FLG_NEG, ALU_ALU_HH_f}));  // open: G, P
  IC_74574 JCU_REG (.D({{7{1'b1}}, JCU_MUL_w[0]}), .CP(OPC_JCR), .OE(OPC_PF), .O(JCU_REG_o), .val(out_74));
  IC_7408 JCU_NAND_D (.A(JCU_REG_o[0]), .B(STEP_4), .Q(ACT_PF));
  IC_74574 ALU_REG_G_L (
    .D({ALU_ALU_LH_f, ALU_ALU_LL_f}), .CP(STEP_IGR), .OE(1'b0), .O(BUS_DATA_OUT_t[7:0]), .val(out_26));
  IC_74574 ALU_REG_G_H (
    .D({FLG_NEG, ALU_ALU_HH_f, ALU_ALU_HL_f}), .CP(STEP_IGR), .OE(1'b0), .O(BUS_DATA_OUT_t[15:8]),
    .val(out_30));
  IC_74670 PF_FILE_LL (
    .RA(BUS_FRA), .WA(BUS_FWA), .WE(ACT_PF), .D(BUS_DATA_OUT_t[3:0]), .RE(1'b0), .val3(out_44),
    .val2(out_42), .Q(BUS_ADR[3:0]), .val1(out_39), .val0(out_37));
  IC_74670 PF_FILE_LH (
    .RA(BUS_FRA), .WA(BUS_FRA), .WE(ACT_PF), .D(BUS_DATA_OUT_t[7:4]), .RE(1'b0), .val3(out_52),
    .val2(out_50), .Q(BUS_ADR[7:4]), .val1(out_48), .val0(out_46));
  IC_74670 PF_FILE_HL (
    .RA(BUS_FRA), .WA(BUS_FWA), .WE(ACT_PF), .D(BUS_DATA_OUT_t[11:8]), .RE(1'b0), .val3(out_64),
    .val2(out_61), .Q(BUS_ADR[11:8]), .val1(out_58), .val0(out_55));
  IC_74670 PF_FILE_HH (
    .RA(BUS_FRA), .WA(BUS_FWA), .WE(ACT_PF), .D(BUS_DATA_OUT_t[15:12]), .RE(1'b0), .val3(out_73),
    .val2(out_71), .Q(BUS_ADR[15:12]), .val1(out_69), .val0(out_67));
  IC_74541 PF_BUF_L (.I(BUS_ADR[7:0]), .OE1(SRC_PF), .OE2(1'b0), .Y(BUS_DATA_IN_t[7:0]));
  IC_74541 PF_BUF_H (.I(BUS_ADR[15:8]), .OE1(SRC_PF), .OE2(1'b0), .Y(BUS_DATA_IN_t[15:8]));
  IC_74161 IC_CNT (
    .LD(1'b0), .D(4'b1111), .CLK(ACT_INT_E), .CLR(ACT_INT_S), .ENT(1'b1), .ENP(1'b1), .val(out_75), .CO(INTM));  // open: Q
  IC_7408 IEU_AND_A (.A(ACT_OP_CIN), .B(FLG_CO), .Q(ACT_ALU_CIN));
  IC_7400 IEU_NAND_A (.A(OPC_DVR), .B(OPC_DVR), .Q(IEU_NAND_A_q));
  IC_7400 IEU_NAND_B (.A(OPC_INTC), .B(OPC_INTC), .Q(IEU_NAND_B_q));
  IC_7408 IEU_AND_B (.A(BUS_ARGO[0]), .B(IEU_NAND_A_q), .Q(ACT_DV_L));
  IC_7408 IEU_AND_C (.A(IEU_NAND_A_q), .B(BUS_ARGO[1]), .Q(ACT_DV_H));
  IC_7400 IEU_NAND_C (.A(BUS_ARGO[0]), .B(IEU_NAND_B_q), .Q(ACT_INT_E));
  IC_7400 IEU_NAND_D (.A(IEU_NAND_B_q), .B(BUS_ARGO[1]), .Q(IEU_NAND_D_q));
  IC_74574 IEU_REG_I_L (
    .D(BUS_DATA_IN_t[7:0]), .CP(STEP_1), .OE(STEP_CNTI_M), .O({BUS_ARGS, ACT_OP_CIN, BUS_OP}), .val(out_13));
  IC_74574 IEU_REG_I_H (
    .D(BUS_DATA_IN_t[15:8]), .CP(STEP_1), .OE(STEP_CNTI_M),
    .O({IEU_REG_I_H_o[7:5], BUS_ARGO, IEU_REG_I_H_o[2:0]}), .val(out_22));
  IC_7408 IEU_AND_D (.A(IEU_NAND_D_q), .B(INTL), .Q(ACT_INT_S));
  IC_74541 IC_BUF_SRC (
    .I({4'b1111, BUS_ARGO, BUS_ARGS}), .OE1(STEP_SRCR), .OE2(1'b0), .Y({IC_BUF_SRC_y, BUS_FWA, BUS_FRA}));
  IC_74541 IC_BUF_IM (
    .I({4'b1111, INTM, 1'b0, INTM, 1'b0}), .OE1(STEP_IMR), .OE2(1'b0), .Y({IC_BUF_IM_y, BUS_FWA, BUS_FRA}));
  Pull_Resistor pull_resistor_1 (.node({IEU_REG_I_H_o[7:5], BUS_ARGO, IEU_REG_I_H_o[2:0], BUS_ARGS, ACT_OP_CIN, BUS_OP}));
  IC_7408 SCU_AND_A (.A(STEP_3), .B(STEP_5), .Q(STEP_IGR));
  IC_7408 SCU_AND_C (.A(CLK_T1), .B(STEP_1), .Q(SCU_AND_C_q));
  IC_74161 SCU_CNT (
    .LD(1'b1), .D(4'b1111), .CLK(CLK), .CLR(1'b1), .ENT(CLK_EN), .ENP(1'b1), .val(out_59),
    .Q({CLK_T8, SCU_CNT_q}), .CO(CLK_T16));
  IC_7400 SCU_NAND_A (.A(STEP_3), .B(STEP_4), .Q(STEP_CNTI_M));
  IC_7408 SCU_AND_D (.A(SCU_AND_C_q), .B(STEP_2), .Q(STEP_IMR));
  IC_74574 IEU_DV_L (
    .D({BUS_ARGS, ACT_OP_CIN, BUS_OP}), .CP(ACT_DV_L), .OE(SRC_DVR), .O(BUS_DATA_IN_t[7:0]), .val(out_14));
  IC_74574 IEU_DV_H (
    .D({BUS_ARGS, ACT_OP_CIN, BUS_OP}), .CP(ACT_DV_H), .OE(SRC_DVR), .O(BUS_DATA_IN_t[15:8]), .val(out_17));
  IC_74138 IEU_DCD_SRC (
    .EN3(1'b0), .D(IEU_REG_I_H_o[2:0]), .EN1(1'b1), .EN2(STEP_SRCR), .Y0(SRC_PF), .Y2(SRC_RF), .Y3(SRC_SF),
    .Y5(SRC_DVR), .Y6(SRC_ADRD), .Y7(SRC_INTB));  // open: Y1, Y4
  IC_74138 IEU_DCD_OPC (
    .EN3(1'b0), .D(IEU_REG_I_H_o[7:5]), .EN1(1'b1), .EN2(STEP_OPCE), .Y0(OPC_PF), .Y1(OPC_A), .Y2(OPC_RF),
    .Y3(OPC_SF), .Y4(OPC_JCR), .Y5(OPC_DVR), .Y6(W), .Y7(OPC_INTC));
  IC_7400 SCU_NAND_B (.A(STEP_IMR), .B(STEP_IMR), .Q(STEP_SRCR));
  IC_7400 SCU_NAND_C (.A(STEP_IMR), .B(SRC_ADRD), .Q(ACT_OUTPUT_M));
  IC_7400 SCU_NAND_D (.A(ACT_OUTPUT_M), .B(ACT_OUTPUT_M), .Q(R));
  IC_74138 SCU_DCD (
    .EN3(1'b0), .D(SCU_CNT_q), .EN1(1'b1), .EN2(1'b0), .Y0(CLK_T1), .Y1(STEP_1), .Y2(STEP_2), .Y3(STEP_3),
    .Y4(STEP_4), .Y5(STEP_5), .Y6(STEP_6), .Y7(STEP_7));
  IC_7408 SCU_AND_B (.A(STEP_4), .B(STEP_6), .Q(STEP_OPCE));
  IC_74541 IC_BUF_INT (
    .I({INT_7, INT_6, INT_5, INT_4, INT_3, INT_2, INT_1, INT_0}), .OE1(SRC_INTB), .OE2(1'b0),
    .Y(BUS_DATA_IN_t[7:0]));
  IC_74670 SF_FILE_L (
    .RA(BUS_FRA), .WA(BUS_FWA), .WE(OPC_SF), .D(BUS_DATA_OUT_t[3:0]), .RE(1'b0), .val3(out_21),
    .val2(out_19), .Q(BUS_SCT[3:0]), .val1(out_16), .val0(out_15));
  IC_74670 SF_FILE_H (
    .RA(BUS_FRA), .WA(BUS_FRA), .WE(OPC_SF), .D(BUS_DATA_OUT_t[7:4]), .RE(1'b0), .val3(out_27),
    .val2(out_25), .Q(BUS_SCT[7:4]), .val1(out_24), .val0(out_23));
  IC_74541 IOU_BUF_OUT_L (.I(BUS_DATA_OUT_t[7:0]), .OE1(ACT_OUTPUT_M), .OE2(1'b0), .Y(BUS_DATA_OUT[7:0]));
  IC_74541 IOU_BUF_OUT_H (.I(BUS_DATA_OUT_t[15:8]), .OE1(ACT_OUTPUT_M), .OE2(1'b0), .Y(BUS_DATA_OUT[15:8]));
  IC_74541 IOU_BUF_IN_L (.I(BUS_DATA_IN[7:0]), .OE1(R), .OE2(1'b0), .Y(BUS_DATA_IN_t[7:0]));
  IC_74541 IOU_BUF_IN_H (.I(BUS_DATA_IN[15:8]), .OE1(R), .OE2(1'b0), .Y(BUS_DATA_IN_t[15:8]));
  IC_74541 SF_BUF (.I(BUS_SCT), .OE1(SRC_SF), .OE2(1'b0), .Y(BUS_DATA_IN_t[7:0]));

  // Other names for the same wires on the sheet: FLG_INTM = INTM; BUS_OP[5] = ACT_OP_CIN; ACT_INPUT_M = R;
  //   OPC_ADRD = W; STEP_0 = CLK_T1; STEP_12 = STEP_4; STEP_CNTI = STEP_4; STEP_IIR = STEP_1

  // Notes on the sheet:
  //   ALU (8 IC)
  //   RFU (4 IC)
  //   JCU (3 IC)
  //   PFU (6 IC)
  //   ICU (4 IC)
  //   IEU (8 IC)
  //   SCU (4 IC)
  //   SFU (3 IC)
  //   IOU (4 IC)
  //   44 IC
  //   2 MIPS
  //   PC MEM 64KB
  //   AP MEM 16MB
  //   Jednostava16
  //   28.10.2026.
  //   Ivan Jonjic (IJPantic on github)
endmodule

module Jednostava8_CPU (
  input  [7:0] BUS_DATA_IN,
  input  INTL,
  input  CLK_EN,
  input  CLK,
  output [7:0] out_5,
  output [7:0] out_6,
  output [3:0] out_7,
  output [3:0] out_8,
  output [3:0] out_9,
  output [7:0] out_10,
  output [3:0] out_11,
  output [3:0] out_12,
  output [3:0] BUS_SCT,
  output [7:0] out_14,
  output [3:0] out_15,
  output [7:0] out_16,
  output [7:0] BUS_DATA_OUT,
  output [3:0] out_18,
  output [3:0] out_19,
  output [3:0] out_20,
  output [3:0] out_21,
  output W,
  output [7:0] BUS_ADR,
  output [3:0] out_24,
  output [3:0] out_25,
  output [3:0] out_26,
  output [3:0] out_27,
  output [3:0] out_28,
  output [3:0] out_29,
  output [3:0] out_30,
  output [3:0] out_31,
  output [3:0] out_32,
  output [3:0] out_33,
  output [3:0] out_34,
  output [3:0] out_35,
  output R,
  output [7:0] out_37,
  output [3:0] out_38,
  output CLK_T16,
  output CLK_T1,
  output CLK_T8,
  output [3:0] out_42,
  output INTM
);

  wire ACT_ALU_CIN, ACT_DV, ACT_INT_E, ACT_INT_S, ACT_JMP, ACT_OP_CIN, ACT_OUTPUT_M, ACT_PF, ALU_ALU_L_co,
       FLG_CO, FLG_EQU, FLG_EQU_LH, FLG_EQU_LL, FLG_NEG, ic_7408_1_q, IEU_NAND_A_q, IEU_NAND_B_q,
       IEU_NAND_D_q, OPC_A, OPC_DVR, OPC_INTC, OPC_JCR, OPC_PF, OPC_RF, OPC_SF, SCU_AND_A_q, SCU_AND_B_q,
       SCU_AND_C_q, SCU_AND_D_q, SCU_AND_F_q, SCU_AND_H_q, SCU_AND_K_q, SCU_AND_L_q, SRC_ADRD, SRC_DVR,
       SRC_INTB, SRC_PF, SRC_RF, SRC_SF, STEP_1, STEP_2, STEP_3, STEP_4, STEP_5, STEP_6, STEP_7, STEP_8,
       STEP_9, STEP_10, STEP_11, STEP_12, STEP_13, STEP_14, STEP_15, STEP_CNTI_M, STEP_IGR, STEP_IMR,
       STEP_OPCE, STEP_SRCR;
  wire [0:0] JCU_MUL_w;
  wire [1:0] BUS_ARGO, BUS_ARGS, BUS_FRA, BUS_FWA;
  wire [2:0] ALU_ALU_H_f, SCU_CNT_q;
  wire [3:0] ALU_ALU_L_f;
  wire [4:0] BUS_OP;
  wire [7:0] ALU_REG_A_L_o, BUS_DATA_IN_t, BUS_DATA_OUT_t, IEU_REG_I_H_o;
  wire [7:1] JCU_REG_o;
  wire [7:4] IC_BUF_IM_y, IC_BUF_SRC_y, undriven;

  IC_74161 IC_CNT (
    .LD(1'b0), .D(4'b1111), .CLK(ACT_INT_E), .CLR(ACT_INT_S), .ENT(1'b1), .ENP(1'b1), .val(out_42), .CO(INTM));  // open: Q
  IC_74574 ALU_REG_A_L (.D(BUS_DATA_IN_t), .CP(OPC_A), .OE(1'b0), .O(ALU_REG_A_L_o), .val(out_16));
  IC_74670 RF_FILE_LL (
    .RA(BUS_FRA), .WA(BUS_FWA), .WE(OPC_RF), .D(BUS_DATA_OUT_t[3:0]), .RE(SRC_RF), .val3(out_26),
    .val2(out_24), .Q(BUS_DATA_IN_t[3:0]), .val1(out_20), .val0(out_18));
  IC_74670 RF_FILE_LH (
    .RA(BUS_FRA), .WA(BUS_FRA), .WE(OPC_RF), .D(BUS_DATA_OUT_t[7:4]), .RE(SRC_RF), .val3(out_34),
    .val2(out_32), .Q(BUS_DATA_IN_t[7:4]), .val1(out_30), .val0(out_28));
  IC_74151 JCU_MUL (
    .S({1'b1, BUS_ARGO}), .D0(FLG_NEG), .D1(FLG_CO), .D2(FLG_EQU), .D3(INTM), .D4(1'b1), .D5(1'b1),
    .D6(1'b1), .D7(1'b1), .EN(1'b0), .W(JCU_MUL_w[0]));  // open: Y
  IC_7408 ic_7408_1 (.A(STEP_CNTI_M), .B(STEP_IMR), .Q(ic_7408_1_q));
  IC_74541 IC_BUF_SRC (
    .I({4'b1111, BUS_ARGO, BUS_ARGS}), .OE1(STEP_SRCR), .OE2(1'b0), .Y({IC_BUF_SRC_y, BUS_FWA, BUS_FRA}));
  IC_74541 IC_BUF_IM (
    .I({4'b1111, INTM, 1'b0, INTM, 1'b0}), .OE1(ic_7408_1_q), .OE2(1'b0), .Y({IC_BUF_IM_y, BUS_FWA, BUS_FRA}));
  IC_74181 ALU_ALU_L (
    .CIN(ACT_ALU_CIN), .M(BUS_OP[4]), .A(BUS_DATA_IN_t[3:0]), .S(BUS_OP[3:0]), .B(ALU_REG_A_L_o[3:0]),
    .AEQB(FLG_EQU_LL), .CO(ALU_ALU_L_co), .val(out_9), .F(ALU_ALU_L_f));  // open: G, P
  IC_74181 ALU_ALU_H (
    .CIN(ALU_ALU_L_co), .M(BUS_OP[4]), .A(BUS_DATA_IN_t[7:4]), .S(BUS_OP[3:0]), .B(ALU_REG_A_L_o[7:4]),
    .AEQB(FLG_EQU_LH), .CO(FLG_CO), .val(out_15), .F({FLG_NEG, ALU_ALU_H_f}));  // open: G, P
  IC_74574 JCU_REG (.D({{7{1'b1}}, JCU_MUL_w[0]}), .CP(OPC_JCR), .OE(OPC_PF), .O({JCU_REG_o, ACT_JMP}), .val(out_37));
  IC_74574 ALU_REG_G (
    .D({FLG_NEG, ALU_ALU_H_f, ALU_ALU_L_f}), .CP(STEP_IGR), .OE(1'b0), .O(BUS_DATA_OUT_t), .val(out_14));
  IC_74670 PF_FILE_LL (
    .RA(BUS_FRA), .WA(BUS_FWA), .WE(ACT_PF), .D(BUS_DATA_OUT_t[3:0]), .RE(1'b0), .val3(out_27),
    .val2(out_25), .Q(BUS_ADR[3:0]), .val1(out_21), .val0(out_19));
  IC_74670 PF_FILE_LH (
    .RA(BUS_FRA), .WA(BUS_FRA), .WE(ACT_PF), .D(BUS_DATA_OUT_t[7:4]), .RE(1'b0), .val3(out_35),
    .val2(out_33), .Q(BUS_ADR[7:4]), .val1(out_31), .val0(out_29));
  IC_74541 PF_BUF_L (.I(BUS_ADR), .OE1(SRC_PF), .OE2(1'b0), .Y(BUS_DATA_IN_t));
  IC_7408 JCU_NAND_B (.A(FLG_EQU_LL), .B(FLG_EQU_LH), .Q(FLG_EQU));
  IC_7408 IEU_AND_C (.A(ACT_OP_CIN), .B(FLG_CO), .Q(ACT_ALU_CIN));
  IC_7408 SCU_AND_A (.A(STEP_5), .B(STEP_6), .Q(SCU_AND_A_q));
  IC_7408 SCU_AND_C (.A(STEP_13), .B(STEP_14), .Q(SCU_AND_C_q));
  IC_7408 SCU_AND_K (.A(STEP_11), .B(STEP_12), .Q(SCU_AND_K_q));
  IC_7408 SCU_AND_L (.A(STEP_3), .B(STEP_4), .Q(SCU_AND_L_q));
  IC_7408 SCU_AND_F (.A(STEP_3), .B(STEP_11), .Q(SCU_AND_F_q));
  IC_7408 SCU_AND_H (.A(STEP_4), .B(STEP_12), .Q(SCU_AND_H_q));
  IC_7408 IEU_AND_D (.A(BUS_ARGO[0]), .B(IEU_NAND_A_q), .Q(ACT_DV));
  IC_7400 IEU_NAND_A (.A(OPC_DVR), .B(OPC_DVR), .Q(IEU_NAND_A_q));
  IC_7400 IEU_NAND_B (.A(OPC_INTC), .B(OPC_INTC), .Q(IEU_NAND_B_q));
  IC_74161 SCU_CNT (
    .LD(1'b1), .D(4'b1111), .CLK(CLK), .CLR(1'b1), .ENT(CLK_EN), .ENP(1'b1), .val(out_38),
    .Q({CLK_T8, SCU_CNT_q}), .CO(CLK_T16));
  IC_7400 SCU_NAND_A (.A(SCU_AND_K_q), .B(SCU_AND_L_q), .Q(STEP_CNTI_M));
  IC_7408 SCU_AND_G (.A(SCU_AND_F_q), .B(STEP_13), .Q(STEP_IGR));
  IC_7408 SCU_AND_I (.A(SCU_AND_H_q), .B(STEP_14), .Q(STEP_OPCE));
  IC_7400 IEU_NAND_C (.A(BUS_ARGO[0]), .B(IEU_NAND_B_q), .Q(ACT_INT_E));
  IC_7400 IEU_NAND_D (.A(IEU_NAND_B_q), .B(BUS_ARGO[1]), .Q(IEU_NAND_D_q));
  IC_7408 SCU_AND_B (.A(SCU_AND_A_q), .B(STEP_7), .Q(SCU_AND_B_q));
  IC_7408 SCU_AND_D (.A(SCU_AND_C_q), .B(STEP_15), .Q(SCU_AND_D_q));
  IC_74574 IEU_REG_I_L (
    .D(BUS_DATA_IN_t), .CP(STEP_1), .OE(STEP_CNTI_M), .O({BUS_ARGS, ACT_OP_CIN, BUS_OP}), .val(out_5));
  IC_74574 IEU_REG_I_H (
    .D(BUS_DATA_IN_t), .CP(STEP_9), .OE(STEP_CNTI_M), .O({IEU_REG_I_H_o[7:5], BUS_ARGO, IEU_REG_I_H_o[2:0]}),
    .val(out_10));
  IC_7408 IEU_AND_A (.A(IEU_NAND_D_q), .B(INTL), .Q(ACT_INT_S));
  IC_7400 SCU_NAND_B (.A(SCU_AND_B_q), .B(SCU_AND_D_q), .Q(STEP_SRCR));
  Pull_Resistor pull_resistor_1 (.node({IEU_REG_I_H_o[7:5], BUS_ARGO, IEU_REG_I_H_o[2:0], BUS_ARGS, ACT_OP_CIN, BUS_OP}));
  // IC_7408 SCU_AND_E: pin names not known
  IC_7406 ic_7406_1 (.A(STEP_SRCR), .Q(STEP_IMR));
  IC_7400 SCU_NAND_C (.A(STEP_IMR), .B(SRC_ADRD), .Q(ACT_OUTPUT_M));
  IC_7400 SCU_NAND_D (.A(ACT_OUTPUT_M), .B(ACT_OUTPUT_M), .Q(R));
  IC_74138 SCU_DCD_L (
    .EN3(1'b0), .D(SCU_CNT_q), .EN1(1'b1), .EN2(CLK_T8), .Y0(CLK_T1), .Y1(STEP_1), .Y2(STEP_2), .Y3(STEP_3),
    .Y4(STEP_4), .Y5(STEP_5), .Y6(STEP_6), .Y7(STEP_7));
  IC_74138 SCU_DCD_H (
    .EN3(1'b0), .D(SCU_CNT_q), .EN1(CLK_T8), .EN2(1'b0), .Y0(STEP_8), .Y1(STEP_9), .Y2(STEP_10),
    .Y3(STEP_11), .Y4(STEP_12), .Y5(STEP_13), .Y6(STEP_14), .Y7(STEP_15));
  IC_74574 IEU_DV_L (.D({BUS_ARGS, ACT_OP_CIN, BUS_OP}), .CP(ACT_DV), .OE(SRC_DVR), .O(BUS_DATA_IN_t), .val(out_6));
  IC_74138 IEU_DCD_SRC (
    .EN3(1'b0), .D(IEU_REG_I_H_o[2:0]), .EN1(1'b1), .EN2(STEP_SRCR), .Y0(SRC_PF), .Y2(SRC_RF), .Y3(SRC_SF),
    .Y5(SRC_DVR), .Y6(SRC_ADRD), .Y7(SRC_INTB));  // open: Y1, Y4
  IC_74138 IEU_DCD_OPC (
    .EN3(1'b0), .D(IEU_REG_I_H_o[7:5]), .EN1(1'b1), .EN2(STEP_OPCE), .Y0(OPC_PF), .Y1(OPC_A), .Y2(OPC_RF),
    .Y3(OPC_SF), .Y4(OPC_JCR), .Y5(OPC_DVR), .Y6(W), .Y7(OPC_INTC));
  IC_7408 SCU_AND_J (.A(ACT_JMP), .B(STEP_12), .Q(ACT_PF));
  IC_74670 SF_FILE (
    .RA(BUS_FRA), .WA(BUS_FWA), .WE(OPC_SF), .D(BUS_DATA_OUT_t[3:0]), .RE(1'b0), .val3(out_12),
    .val2(out_11), .Q(BUS_SCT), .val1(out_8), .val0(out_7));
  IC_74541 IOU_BUF_OUT_L (.I(BUS_DATA_OUT_t), .OE1(ACT_OUTPUT_M), .OE2(1'b0), .Y(BUS_DATA_OUT));
  IC_74541 IOU_BUF_IN_L (.I(BUS_DATA_IN), .OE1(R), .OE2(1'b0), .Y(BUS_DATA_IN_t));
  IC_74541 SF_BUF (.I({undriven, BUS_SCT}), .OE1(SRC_SF), .OE2(1'b0), .Y(BUS_DATA_IN_t));

  // Other names for the same wires on the sheet: FLG_INTM = INTM; BUS_OP[5] = ACT_OP_CIN; ACT_INPUT_M = R;
  //   OPC_ADRD = W; STEP_0 = CLK_T1; STEP_CNTI = STEP_12; STEP_IIR_H = STEP_9; STEP_IIR_L = STEP_1

  // Notes on the sheet:
  //   ALU (4 IC)
  //   RFU (2 IC)
  //   JCU (2 IC)
  //   ICU (3 IC)
  //   PFU (3 IC)
  //   IEU (7 IC)
  //   SCU (7 IC)
  //   SFU (2 IC)
  //   IOU (2 IC)
  //   32 IC
  //   1 MIPS
  //   PC MEM 256B
  //   AP MEM 4KB
  //   Jednostava8
  //   28.10.2026.
  //   Ivan Jonjic (IJPantic on github)
endmodule
