// Logisim project Semafor.circ as structural Verilog: 1 circuit, main circuit main
module main (
  output [3:0] out_1,
  output [3:0] out_2,
  output [3:0] out_3,
  output [3:0] out_4,
  output [3:0] out_5,
  output [3:0] out_6,
  output [3:0] out_7,
  output [3:0] out_8,
  output [3:0] out_9,
  output [3:0] out_10,
  output [3:0] out_11,
  output [3:0] out_12,
  output [3:0] out_13,
  output [3:0] out_14,
  output [3:0] out_15,
  output [3:0] out_16,
  output [3:0] out_17,
  output [3:0] out_18,
  output [3:0] out_19,
  output [3:0] out_20,
  output [3:0] out_21,
  output [3:0] out_22,
  output [3:0] out_23,
  output [3:0] out_24,
  output [3:0] out_25,
  output [3:0] out_26,
  output [3:0] out_27,
  output [3:0] out_28,
  output [3:0] out_29,
  output [3:0] out_30,
  output [3:0] out_31,
  output [3:0] out_32,
  output [3:0] out_33,
  output [3:0] out_34,
  output [3:0] out_35,
  output [3:0] out_36,
  output [3:0] out_37,
  output [3:0] out_38,
  output [3:0] out_39,
  output [3:0] out_40,
  output [7:0] out_41,
  output [3:0] out_42,
  output [3:0] out_43,
  output [7:0] out_44,
  output [7:0] out_45,
  output [7:0] out_46,
  output [7:0] out_47,
  output [7:0] out_48,
  output [7:0] out_49,
  output [3:0] out_50,
  output [3:0] out_51,
  output [3:0] out_52,
  output [3:0] out_53,
  output [7:0] out_54,
  output [7:0] out_55,
  output [7:0] out_56,
  output [7:0] IO_OUTPUT
);

  wire CE_IO, CE_ROM, clk_out, ic_7432_1_q, jednostava16_cpu_1_p60, jednostava16_cpu_1_p61,
       jednostava16_cpu_1_p64, nor_1_out;
  wire [7:0] jednostava16_cpu_1_p63;
  wire [15:0] jednostava16_cpu_1_p58, jednostava16_cpu_1_p62, rom_1_data;

  Clock clk (.out(clk_out));
  // Jednostava16_CPU jednostava16_cpu_1: pin names not known; wires that end beside it: clk_out, 1'b1, out_1, out_11, out_21, out_31, out_48, out_2, out_12, out_22, out_32, out_41, out_46, out_49, out_3, out_13, out_23, out_33, out_4, out_14, out_24, out_34, out_42, out_50, out_5, out_15, out_25, out_35, out_51, out_6, out_16, out_26, out_36, out_43, out_47, out_52, out_53, out_7, out_17, out_27, out_37, out_44, out_8, out_18, out_28, out_38, out_45, out_54, out_9, out_19, out_29, out_39, out_55, out_10, out_20, out_30, out_40, jednostava16_cpu_1_p58, jednostava16_cpu_1_p58, jednostava16_cpu_1_p60, jednostava16_cpu_1_p61, jednostava16_cpu_1_p62, jednostava16_cpu_1_p63, jednostava16_cpu_1_p64
  IC_74138 sct_dcd (
    .EN3(jednostava16_cpu_1_p63[4]), .D(jednostava16_cpu_1_p63[2:0]), .EN1(1'b1),
    .EN2(jednostava16_cpu_1_p63[3]), .Y0(CE_ROM), .Y1(CE_IO));  // open: Y2, Y3, Y4, Y5, Y6, Y7
  ROM #(.dataWidth(16)) rom_1 (.addr(jednostava16_cpu_1_p62[7:0]), .data(rom_1_data));
  IC_7432 ic_7432_1 (.A(CE_IO), .B(jednostava16_cpu_1_p61), .Q(ic_7432_1_q));
  Button #(.press("passive")) button_1 (.out(jednostava16_cpu_1_p64));
  IC_74574 output_reg (.D(jednostava16_cpu_1_p58[7:0]), .CP(ic_7432_1_q), .OE(1'b0), .O(IO_OUTPUT), .val(out_56));
  nor nor_1 (nor_1_out, CE_ROM, jednostava16_cpu_1_p60);
  assign jednostava16_cpu_1_p58 = nor_1_out ? rom_1_data : 16'bz;  // Controlled_Buffer controlled_buffer_1
  LED led_1 (.in(IO_OUTPUT[0]));
  LED led_2 (.in(IO_OUTPUT[1]));
  LED led_3 (.in(IO_OUTPUT[2]));
  LED led_4 (.in(IO_OUTPUT[3]));
  LED led_5 (.in(IO_OUTPUT[4]));

  // Notes on the sheet:
  //   contents of rom_1 (hex, n*v repeats v):
  //   e800 a801 7d20 a80f 520 a809 c5e0 a80a c5e0 a80c c5e0 a80a c5e0 a805 1520 a811 c5e0 a800 520
  //   VOZILA
  //   PJEŠACI
endmodule
