// Logisim project LIB_MMU.circ as structural Verilog: 1 circuit, main circuit MMU
module MMU (
  input  ACT_CIN,
  input  [15:0] BUS_DATA,
  input  ACT_W_L,
  input  ACT_EN,
  input  ACT_W_H,
  input  [23:0] BUS_ADR_IN,
  output [7:0] out_7,
  output [3:0] out_8,
  output [3:0] out_9,
  output [7:0] out_10,
  output [3:0] out_11,
  output ACT_CO,
  output [23:0] BUS_ADR_OUT
);

  wire MMU_ADD_H_co, MMU_ADD_M_co;
  wire [7:0] MMU_REG_H_o, MMU_REG_L_o;

  IC_74574 MMU_REG_L (.D(BUS_DATA[7:0]), .CP(ACT_W_L), .OE(ACT_EN), .O(MMU_REG_L_o), .val(out_7));
  Pull_Resistor pull_resistor_1 (.node(MMU_REG_L_o));
  IC_74574 MMU_REG_H (.D(BUS_DATA[7:0]), .CP(ACT_W_H), .OE(ACT_EN), .O(MMU_REG_H_o), .val(out_10));
  Pull_Resistor pull_resistor_2 (.node(MMU_REG_H_o));
  IC_74283 MMU_ADD_H (
    .CIN(ACT_CIN), .A(MMU_REG_L_o[3:0]), .B(BUS_ADR_IN[15:12]), .CO(MMU_ADD_H_co), .val(out_8),
    .SUM(BUS_ADR_OUT[15:12]));
  IC_74283 MMU_ADD_M (
    .CIN(MMU_ADD_H_co), .A(MMU_REG_L_o[7:4]), .B(BUS_ADR_IN[19:16]), .CO(MMU_ADD_M_co), .val(out_9),
    .SUM(BUS_ADR_OUT[19:16]));
  IC_74283 MMU_ADD_L (
    .CIN(MMU_ADD_M_co), .A(MMU_REG_H_o[3:0]), .B(BUS_ADR_IN[23:20]), .CO(ACT_CO), .val(out_11),
    .SUM(BUS_ADR_OUT[23:20]));

  assign BUS_ADR_OUT[11:0] = BUS_ADR_IN[11:0];
endmodule
